// Logisim project dolezity_projekt_do__skoly.circ as structural Verilog: 1 circuit, main circuit main
module main (
  input  in_1,
  input  in_2,
  input  in_3
);

  wire and_1_out, and_2_out, and_3_out, and_4_out, and_5_out, and_6_out, and_7_out, and_8_out, and_9_out,
       and_10_out, and_11_out, and_12_out, and_13_out, and_14_out, and_15_out, and_16_out, and_17_out,
       and_18_out, clock_1_out, d_ff_1_qn, d_ff_2_q, d_ff_3_q, d_ff_4_q, d_ff_5_q, not_1_out, not_2_out,
       not_3_out, not_4_out, not_5_out, not_6_out, not_7_out, not_8_out, not_9_out, not_10_out, not_11_out,
       not_12_out, or_1_out, or_2_out, or_3_out, or_4_out, or_5_out, or_6_out, or_7_out, or_8_out, or_13_out,
       or_14_out, or_15_out, or_16_out, or_17_out, or_18_out, or_19_out, or_20_out, pull_resistor_5_node,
       pull_resistor_6_node, pull_resistor_7_node, pull_resistor_8_node, pull_resistor_9_node,
       pull_resistor_11_node, pull_resistor_13_node, pull_resistor_15_node, pull_resistor_17_node,
       pull_resistor_18_node, pull_resistor_19_node, pull_resistor_20_node, pull_resistor_21_node,
       pull_resistor_22_node, pull_resistor_23_node, pull_resistor_30_node, pull_resistor_35_node,
       s_r_ff_1_q, s_r_ff_2_q, s_r_ff_3_q, s_r_ff_4_q, s_r_ff_5_q, s_r_ff_6_q, s_r_ff_7_q, s_r_ff_8_q,
       t_ff_1_q, t_ff_1_qn, t_ff_2_q, t_ff_2_qn, t_ff_3_q, t_ff_3_qn, t_ff_4_q, t_ff_4_qn, transistor_1_out,
       transistor_2_out, transistor_3_out, transistor_4_out, transistor_6_out, transistor_8_out,
       transistor_10_out, transistor_12_out, transistor_21_out, transistor_25_out, transistor_26_out,
       transistor_27_out, transistor_28_out, transistor_29_out, transistor_30_out, transistor_31_out,
       transistor_33_out, transistor_34_out, xor_1_out, xor_2_out, xor_3_out, xor_4_out, xor_5_out,
       xor_6_out, xor_7_out, xor_8_out;
  wire [3:0] or_9_out;

  or or_1 (or_1_out, pull_resistor_20_node, pull_resistor_19_node, pull_resistor_18_node, pull_resistor_17_node);
  not not_1 (not_1_out, or_1_out);
  Clock clock_1 (.out(clock_1_out));
  D_Flip_Flop d_ff_1 (.D(or_8_out), .clk(clock_1_out), .Qn(d_ff_1_qn));  // open: Q, preset, reset
  or or_2 (or_2_out, in_2, pull_resistor_20_node);
  not not_2 (not_2_out, clock_1_out);
  Transistor transistor_1 (.in(or_2_out), .out(transistor_1_out), .gate(and_1_out));
  Pull_Resistor pull_resistor_1 (.node(transistor_1_out));
  not not_3 (not_3_out, clock_1_out);
  Transistor transistor_2 (.in(pull_resistor_19_node), .out(transistor_2_out), .gate(and_1_out));
  Pull_Resistor pull_resistor_2 (.node(transistor_2_out));
  not not_4 (not_4_out, clock_1_out);
  Transistor transistor_3 (.in(pull_resistor_18_node), .out(transistor_3_out), .gate(and_1_out));
  Pull_Resistor pull_resistor_3 (.node(transistor_3_out));
  not not_5 (not_5_out, clock_1_out);
  Transistor transistor_4 (.in(pull_resistor_17_node), .out(transistor_4_out), .gate(and_1_out));
  Pull_Resistor pull_resistor_4 (.node(transistor_4_out));
  Pull_Resistor pull_resistor_5 (.node(pull_resistor_5_node));
  Transistor transistor_5 (.in(or_3_out), .out(pull_resistor_5_node), .gate(not_2_out));
  or or_3 (or_3_out, pull_resistor_9_node, transistor_6_out);
  Transistor transistor_6 (.in(transistor_1_out), .out(transistor_6_out), .gate(not_6_out));
  Pull_Resistor pull_resistor_6 (.node(pull_resistor_6_node));
  Transistor transistor_7 (.in(or_4_out), .out(pull_resistor_6_node), .gate(not_3_out));
  or or_4 (or_4_out, pull_resistor_11_node, transistor_8_out);
  Transistor transistor_8 (.in(transistor_2_out), .out(transistor_8_out), .gate(not_7_out));
  Pull_Resistor pull_resistor_7 (.node(pull_resistor_7_node));
  Transistor transistor_9 (.in(or_5_out), .out(pull_resistor_7_node), .gate(not_4_out));
  or or_5 (or_5_out, pull_resistor_13_node, transistor_10_out);
  Transistor transistor_10 (.in(transistor_3_out), .out(transistor_10_out), .gate(not_8_out));
  Pull_Resistor pull_resistor_8 (.node(pull_resistor_8_node));
  Transistor transistor_11 (.in(or_6_out), .out(pull_resistor_8_node), .gate(not_5_out));
  or or_6 (or_6_out, pull_resistor_15_node, transistor_12_out);
  Transistor transistor_12 (.in(transistor_4_out), .out(transistor_12_out), .gate(not_9_out));
  Pull_Resistor pull_resistor_9 (.node(pull_resistor_9_node));
  Transistor transistor_13 (.in(and_1_out), .out(pull_resistor_9_node), .gate(t_ff_1_qn));
  Pull_Resistor pull_resistor_10 (.node(transistor_6_out));
  Pull_Resistor pull_resistor_11 (.node(pull_resistor_11_node));
  Transistor transistor_14 (.in(and_1_out), .out(pull_resistor_11_node), .gate(t_ff_2_qn));
  Pull_Resistor pull_resistor_12 (.node(transistor_8_out));
  Pull_Resistor pull_resistor_13 (.node(pull_resistor_13_node));
  Transistor transistor_15 (.in(and_1_out), .out(pull_resistor_13_node), .gate(t_ff_3_qn));
  Pull_Resistor pull_resistor_14 (.node(transistor_10_out));
  Pull_Resistor pull_resistor_15 (.node(pull_resistor_15_node));
  Transistor transistor_16 (.in(and_1_out), .out(pull_resistor_15_node), .gate(t_ff_4_qn));
  Pull_Resistor pull_resistor_16 (.node(transistor_12_out));
  and and_1 (and_1_out, d_ff_1_qn, or_8_out);
  T_Flip_Flop t_ff_1 (
    .T(clock_1_out), .clk(pull_resistor_5_node), .Q(t_ff_1_q), .Qn(t_ff_1_qn));  // open: reset, preset
  T_Flip_Flop t_ff_2 (
    .T(clock_1_out), .clk(pull_resistor_6_node), .Q(t_ff_2_q), .Qn(t_ff_2_qn));  // open: reset, preset
  T_Flip_Flop t_ff_3 (
    .T(clock_1_out), .clk(pull_resistor_7_node), .Q(t_ff_3_q), .Qn(t_ff_3_qn));  // open: reset, preset
  T_Flip_Flop t_ff_4 (
    .T(clock_1_out), .clk(pull_resistor_8_node), .Q(t_ff_4_q), .Qn(t_ff_4_qn));  // open: reset, preset
  not not_6 (not_6_out, t_ff_1_qn);
  not not_7 (not_7_out, t_ff_2_qn);
  not not_8 (not_8_out, t_ff_3_qn);
  not not_9 (not_9_out, t_ff_4_qn);
  not not_10 (not_10_out, in_1);
  and and_2 (and_2_out, t_ff_4_qn, t_ff_3_qn, t_ff_2_qn, t_ff_1_qn);
  not not_11 (not_11_out, and_2_out);
  Pull_Resistor pull_resistor_17 (.node(pull_resistor_17_node));
  Transistor transistor_17 (.in(s_r_ff_2_q), .out(pull_resistor_17_node), .gate(not_11_out));
  Pull_Resistor pull_resistor_18 (.node(pull_resistor_18_node));
  Transistor transistor_18 (.in(s_r_ff_1_q), .out(pull_resistor_18_node), .gate(not_11_out));
  Pull_Resistor pull_resistor_19 (.node(pull_resistor_19_node));
  Transistor transistor_19 (.in(s_r_ff_4_q), .out(pull_resistor_19_node), .gate(not_11_out));
  Pull_Resistor pull_resistor_20 (.node(pull_resistor_20_node));
  Transistor transistor_20 (.in(s_r_ff_3_q), .out(pull_resistor_20_node), .gate(not_11_out));
  buf xor_1 (xor_1_out, t_ff_1_q);  // XOR_Gate
  buf xor_2 (xor_2_out, t_ff_2_q);  // XOR_Gate
  buf xor_3 (xor_3_out, t_ff_3_q);  // XOR_Gate
  buf xor_4 (xor_4_out, t_ff_4_q);  // XOR_Gate
  and and_3 (and_3_out, and_6_out, xor_2_out);
  and and_4 (and_4_out, and_3_out, xor_3_out);
  and and_5 (and_5_out, and_4_out, xor_4_out);
  or or_7 (or_7_out, and_5_out, xor_5_out);
  xor xor_5 (xor_5_out, xor_1_out, not_10_out);
  Transistor transistor_21 (.in(or_7_out), .out(transistor_21_out), .gate(or_8_out));
  and and_6 (and_6_out, not_10_out, xor_1_out);
  Pull_Resistor pull_resistor_21 (.node(pull_resistor_21_node));
  Transistor transistor_22 (.in(xor_6_out), .out(pull_resistor_21_node), .gate(or_8_out));
  xor xor_6 (xor_6_out, xor_2_out, and_6_out);
  Pull_Resistor pull_resistor_22 (.node(pull_resistor_22_node));
  Transistor transistor_23 (.in(xor_7_out), .out(pull_resistor_22_node), .gate(or_8_out));
  xor xor_7 (xor_7_out, xor_3_out, and_3_out);
  Pull_Resistor pull_resistor_23 (.node(pull_resistor_23_node));
  Transistor transistor_24 (.in(xor_8_out), .out(pull_resistor_23_node), .gate(or_8_out));
  xor xor_8 (xor_8_out, xor_4_out, and_4_out);
  or or_8 (or_8_out, s_r_ff_3_q, s_r_ff_4_q, s_r_ff_1_q, s_r_ff_2_q);
  Transistor transistor_25 (.in(transistor_21_out), .out(transistor_25_out), .gate(and_7_out));
  Pull_Resistor pull_resistor_24 (.node(transistor_25_out));
  Pull_Resistor pull_resistor_25 (.node(transistor_21_out));
  Transistor transistor_26 (.in(pull_resistor_21_node), .out(transistor_26_out), .gate(and_7_out));
  Pull_Resistor pull_resistor_26 (.node(transistor_26_out));
  Transistor transistor_27 (.in(pull_resistor_22_node), .out(transistor_27_out), .gate(and_7_out));
  Pull_Resistor pull_resistor_27 (.node(transistor_27_out));
  Transistor transistor_28 (.in(pull_resistor_23_node), .out(transistor_28_out), .gate(and_7_out));
  Pull_Resistor pull_resistor_28 (.node(transistor_28_out));
  and and_7 (and_7_out, not_1_out, or_8_out);
  S_R_Flip_Flop s_r_ff_1 (
    .S(transistor_27_out), .clk(clock_1_out), .R(and_7_out), .Q(s_r_ff_1_q));  // open: Qn, preset, reset
  S_R_Flip_Flop s_r_ff_2 (
    .S(transistor_28_out), .clk(clock_1_out), .R(and_7_out), .Q(s_r_ff_2_q));  // open: Qn, preset, reset
  S_R_Flip_Flop s_r_ff_3 (
    .S(transistor_25_out), .clk(clock_1_out), .R(and_7_out), .Q(s_r_ff_3_q));  // open: Qn, preset, reset
  S_R_Flip_Flop s_r_ff_4 (
    .S(transistor_26_out), .clk(clock_1_out), .R(and_7_out), .Q(s_r_ff_4_q));  // open: Qn, preset, reset
  or or_9 (or_9_out[0], d_ff_2_q, s_r_ff_3_q);
  D_Flip_Flop d_ff_2 (.D(s_r_ff_3_q), .clk(clock_1_out), .Q(d_ff_2_q));  // open: Qn, preset, reset
  or or_10 (or_9_out[1], d_ff_3_q, s_r_ff_4_q);
  D_Flip_Flop d_ff_3 (.D(s_r_ff_4_q), .clk(clock_1_out), .Q(d_ff_3_q));  // open: Qn, preset, reset
  or or_11 (or_9_out[2], d_ff_4_q, s_r_ff_1_q);
  D_Flip_Flop d_ff_4 (.D(s_r_ff_1_q), .clk(clock_1_out), .Q(d_ff_4_q));  // open: Qn, preset, reset
  or or_12 (or_9_out[3], d_ff_5_q, s_r_ff_2_q);
  D_Flip_Flop d_ff_5 (.D(s_r_ff_2_q), .clk(clock_1_out), .Q(d_ff_5_q));  // open: Qn, preset, reset
  Hex_Digit_Display hex_digit_display_1 (.value(or_9_out));  // open: dp
  and and_8 (and_8_out, ~or_9_out[3], ~or_9_out[1], ~or_9_out[2]);  // AND_Gate
  and and_9 (and_9_out, and_8_out, or_9_out[0]);
  and and_10 (and_10_out, or_9_out[2], or_9_out[3]);
  and and_11 (and_11_out, ~or_9_out[0], ~or_9_out[1]);  // AND_Gate
  and and_12 (and_12_out, or_9_out[0], or_9_out[2]);
  and and_13 (and_13_out, ~or_9_out[1], ~or_9_out[3]);  // AND_Gate
  and and_14 (and_14_out, or_9_out[1], or_9_out[0], or_9_out[2]);
  and and_15 (and_15_out, and_10_out, and_11_out);
  and and_16 (and_16_out, and_12_out, and_13_out);
  and and_17 (and_17_out, and_14_out, ~or_9_out[3]);  // AND_Gate
  or or_13 (or_13_out, and_15_out, and_17_out, and_16_out);
  or or_14 (or_14_out, and_9_out, and_17_out, and_15_out);
  or or_15 (or_15_out, and_9_out, and_16_out, and_15_out);
  or or_16 (or_16_out, and_9_out, and_16_out, and_17_out);
  S_R_Flip_Flop s_r_ff_5 (.S(and_9_out), .clk(clock_1_out), .R(or_13_out), .Q(s_r_ff_5_q));  // open: Qn, preset, reset
  S_R_Flip_Flop s_r_ff_6 (.S(and_16_out), .clk(clock_1_out), .R(or_14_out), .Q(s_r_ff_6_q));  // open: Qn, preset, reset
  S_R_Flip_Flop s_r_ff_7 (.S(and_17_out), .clk(clock_1_out), .R(or_15_out), .Q(s_r_ff_7_q));  // open: Qn, preset, reset
  S_R_Flip_Flop s_r_ff_8 (.S(and_15_out), .clk(clock_1_out), .R(or_16_out), .Q(s_r_ff_8_q));  // open: Qn, preset, reset
  or or_17 (or_17_out, s_r_ff_6_q, s_r_ff_8_q);
  or or_18 (or_18_out, s_r_ff_5_q, s_r_ff_6_q);
  Transistor transistor_29 (.in(clock_1_out), .out(transistor_29_out), .gate(not_12_out));
  not not_12 (not_12_out, in_3);
  Transistor transistor_30 (.in(or_18_out), .out(transistor_30_out), .gate(in_3));
  Transistor transistor_31 (.in(s_r_ff_7_q), .out(transistor_31_out), .gate(in_3));
  Pull_Resistor pull_resistor_29 (.node(transistor_31_out));
  Pull_Resistor pull_resistor_30 (.node(pull_resistor_30_node));
  Transistor transistor_32 (.in(or_17_out), .out(pull_resistor_30_node), .gate(in_3));
  Pull_Resistor pull_resistor_31 (.node(transistor_30_out));
  Pull_Resistor pull_resistor_32 (.node(transistor_29_out));
  or or_19 (or_19_out, pull_resistor_30_node, transistor_29_out);
  Transistor transistor_33 (.in(transistor_30_out), .out(transistor_33_out), .gate(in_3));
  Transistor transistor_34 (.in(or_19_out), .out(transistor_34_out), .gate(in_3));
  LED led_1 (.in(transistor_31_out));
  LED led_2 (.in(or_19_out));
  LED led_3 (.in(transistor_30_out));
  Pull_Resistor pull_resistor_33 (.node(transistor_33_out));
  Pull_Resistor pull_resistor_34 (.node(transistor_34_out));
  Pull_Resistor pull_resistor_35 (.node(pull_resistor_35_node));
  Transistor transistor_35 (.in(transistor_31_out), .out(pull_resistor_35_node), .gate(in_3));
  LED led_4 (.in(transistor_33_out));
  LED led_5 (.in(or_20_out));
  and and_18 (and_18_out, ~transistor_33_out, transistor_34_out);  // AND_Gate
  or or_20 (or_20_out, and_18_out, pull_resistor_35_node);

  // Notes on the sheet:
  //   ten final semafor je dost v pravo
  //   update clock
  //   předem se za tohle omlouvám
  //   W
  //   W
  //   W
  //   W
  //   reset memory
  //   R
  //   R
  //   R
  //   R
  //   hodně goofy 4 bit memory
  //   block write
  //   clock
  //   reset M2
  //   0001 -1
  //   0101 - 5
  //   0111 -7
  //   1100 - 12
  //   blikací oranžová tlačítko
  //   semafor konečně
  //   jestli nefunguje tak chvíli počkejte on naskočí
endmodule
